// Logisim project DE-mini-project.circ as structural Verilog: 1 circuit, main circuit main
module main (
  input  [7:0] in_1,
  input  [7:0] in_2,
  input  [7:0] in_3,
  input  [7:0] in_4,
  input  [7:0] in_5,
  input  [7:0] in_6,
  input  [7:0] in_7,
  input  [7:0] in_8,
  input  in_9,
  input  in_10,
  output out_11,
  output out_12,
  output out_13
);

  wire and_1_out, and_2_out, clock_1_out, d_ff_2_qn, d_ff_3_qn, or_1_out, xor_1_out, xor_2_out;
  wire [7:0] multiplexer_1_out;

  xor xor_1 (xor_1_out, out_11, out_13);
  and and_1 (and_1_out, out_11, d_ff_2_qn);
  xor xor_2 (xor_2_out, out_12, out_13);
  and and_2 (and_2_out, xor_1_out, out_12);
  Clock clock_1 (.out(clock_1_out));
  D_Flip_Flop d_ff_1 (.clk(clock_1_out), .D(or_1_out), .Q(out_11), .reset(in_10));  // open: Qn, preset, en
  or or_1 (or_1_out, and_2_out, and_1_out);
  D_Flip_Flop d_ff_2 (.clk(clock_1_out), .D(xor_2_out), .Q(out_12), .Qn(d_ff_2_qn), .reset(in_10));  // open: preset, en
  D_Flip_Flop d_ff_3 (.clk(clock_1_out), .D(d_ff_3_qn), .Q(out_13), .Qn(d_ff_3_qn), .reset(in_10));  // open: preset, en
  Multiplexer #(.select(3), .width(8)) multiplexer_1 (
    .in0(in_1), .in1(in_2), .in2(in_3), .in3(in_4), .in4(in_5), .in5(in_6), .in6(in_7), .in7(in_8),
    .out(multiplexer_1_out), .sel({out_11, out_12, out_13}), .en(in_9));
  LED led_1 (.in(multiplexer_1_out[0]));
  LED led_2 (.in(multiplexer_1_out[6]));
  LED led_3 (.in(multiplexer_1_out[7]));
  LED led_4 (.in(multiplexer_1_out[1]));
  LED led_5 (.in(multiplexer_1_out[2]));
  LED led_6 (.in(multiplexer_1_out[4]));
  LED led_7 (.in(multiplexer_1_out[5]));
  LED led_8 (.in(multiplexer_1_out[3]));
endmodule
