// Logisim project INTERNAL_PRECTICAL_SET-1.circ as structural Verilog: 1 circuit, main circuit main
module main (
  input  E,
  input  X,
  output out_3,
  output out_4
);

  wire clock_1_out, j_k_ff_1_qn, j_k_ff_2_qn, or_1_out, xnor_1_out;

  or or_1 (or_1_out, E, X);
  xnor xnor_1 (xnor_1_out, E, out_4);
  Clock clock_1 (.out(clock_1_out));
  J_K_Flip_Flop j_k_ff_1 (
    .J(xnor_1_out), .clk(clock_1_out), .K(xnor_1_out), .Q(out_3), .Qn(j_k_ff_1_qn));  // open: preset, en, reset
  J_K_Flip_Flop j_k_ff_2 (
    .J(or_1_out), .clk(clock_1_out), .K(or_1_out), .Q(out_4), .Qn(j_k_ff_2_qn));  // open: preset, en, reset
endmodule
