// Logisim project p-7.circ as structural Verilog: 1 circuit, main circuit main
module main (
  output out_1,
  output out_2,
  output out_3,
  output out_4
);

  wire and_1_out, clock_1_out, d_ff_3_qn, d_ff_4_qn, or_1_out, or_2_out;

  and and_1 (and_1_out, out_3, out_2);
  or or_1 (or_1_out, d_ff_3_qn, d_ff_4_qn);
  Clock clock_1 (.out(clock_1_out));
  or or_2 (or_2_out, out_2, out_1, d_ff_4_qn);
  D_Flip_Flop d_ff_1 (.clk(clock_1_out), .D(and_1_out), .Q(out_1));  // open: Qn, preset, en, reset
  D_Flip_Flop d_ff_2 (.clk(clock_1_out), .D(or_1_out), .Q(out_2));  // open: Qn, preset, en, reset
  D_Flip_Flop d_ff_3 (.clk(clock_1_out), .D(out_4), .Q(out_3), .Qn(d_ff_3_qn));  // open: preset, en, reset
  D_Flip_Flop d_ff_4 (.clk(clock_1_out), .D(or_2_out), .Q(out_4), .Qn(d_ff_4_qn));  // open: preset, en, reset
endmodule
