// Logisim project prac3.circ as structural Verilog: 1 circuit, main circuit main
module main (
  input  [3:0] in_1,
  input  [3:0] in_2,
  input  in_3,
  input  [3:0] in_4,
  input  in_5,
  input  [1:0] in_6,
  input  in_7,
  input  [3:0] in_8,
  output out_9,
  output out_10
);

  wire comparator_1_eq, comparator_1_gt, comparator_1_lt;
  wire [3:0] adder_1_out, multiplexer_1_out, subtractor_1_out;

  Subtractor #(.width(4)) subtractor_1 (.a(in_2), .b(in_4), .out(subtractor_1_out), .bin(in_3), .bout(out_9));
  Adder #(.width(4)) adder_1 (.a(in_2), .b(in_8), .out(adder_1_out), .cin(in_7), .cout(out_10));
  Multiplexer #(.select(2), .width(4)) multiplexer_1 (
    .in0(in_2), .in1(subtractor_1_out), .in2(adder_1_out), .out(multiplexer_1_out), .sel(in_6), .en(in_5));  // open: in3
  Comparator #(.width(4)) comparator_1 (
    .a(in_1), .b(multiplexer_1_out), .gt(comparator_1_gt), .eq(comparator_1_eq), .lt(comparator_1_lt));
  LED led_1 (.in(comparator_1_gt));
  LED led_2 (.in(comparator_1_eq));
  LED led_3 (.in(comparator_1_lt));
endmodule
