// Logisim project prac5.circ as structural Verilog: 1 circuit, main circuit main
module main (
  input  in_1,
  output out_2,
  output out_3,
  output out_4,
  output out_5
);

  wire and_1_out, and_2_out, clock_1_out;

  Clock clock_1 (.out(clock_1_out));
  and and_1 (and_1_out, out_3, and_2_out);
  and and_2 (and_2_out, out_5, out_4);
  J_K_Flip_Flop j_k_ff_1 (.J(and_1_out), .clk(clock_1_out), .K(and_1_out), .Q(out_2));  // open: Qn, preset, en, reset
  J_K_Flip_Flop j_k_ff_2 (.J(and_2_out), .clk(clock_1_out), .K(and_2_out), .Q(out_3));  // open: Qn, preset, en, reset
  J_K_Flip_Flop j_k_ff_3 (.J(out_5), .clk(clock_1_out), .K(out_5), .Q(out_4));  // open: Qn, preset, en, reset
  J_K_Flip_Flop j_k_ff_4 (.J(in_1), .clk(clock_1_out), .K(in_1), .Q(out_5));  // open: Qn, preset, en, reset
endmodule
