// Logisim project practical - 2.circ as structural Verilog: 1 circuit, main circuit main
module main (
  input  in_1,
  input  in_2,
  input  [3:0] in_3,
  input  [3:0] in_4,
  input  [3:0] in_5,
  input  [2:0] in_6,
  input  in_7,
  output [3:0] out_8,
  output out_9,
  output out_10,
  output [3:0] out_11,
  output [3:0] out_12
);

  wire [3:0] adder_2_out, divider_1_out, divider_1_rem, multiplier_1_out, subtractor_1_out, subtractor_2_out;

  Adder #(.width(4)) adder_1 (.a(in_3), .b(in_5), .out(out_8), .cin(in_1), .cout(out_9));
  Subtractor #(.width(4)) subtractor_1 (.a(in_3), .b(in_5), .out(subtractor_1_out), .bin(in_2), .bout(out_10));
  Multiplier #(.width(4)) multiplier_1 (.a(in_3), .b(in_5), .out(multiplier_1_out), .cin(in_4), .cout(out_12));
  Divider #(.width(4)) divider_1 (.a(in_3), .b(in_5), .out(divider_1_out), .upper(in_4), .rem(divider_1_rem));
  Adder #(.width(4)) adder_2 (.a(in_3), .b(in_5), .out(adder_2_out));  // open: cin, cout
  Subtractor #(.width(4)) subtractor_2 (.a(in_3), .b(in_5), .out(subtractor_2_out));  // open: bin, bout
  Multiplexer #(.select(3), .width(4)) multiplexer_1 (
    .in0(out_8), .in1(subtractor_1_out), .in2(multiplier_1_out), .in3(divider_1_out), .in4(adder_2_out),
    .in5(subtractor_2_out), .in6(divider_1_rem), .out(out_11), .sel(in_6), .en(in_7));  // open: in7
endmodule
