// Logisim project practical-4(2).circ as structural Verilog: 1 circuit, main circuit main
module main (
  input  [3:0] in_1,
  input  [3:0] in_2,
  input  [3:0] in_3,
  input  [3:0] in_4,
  input  [3:0] in_5,
  input  [3:0] in_6,
  input  [3:0] in_7,
  input  in_8,
  input  [1:0] in_9,
  input  in_10,
  input  [3:0] in_11,
  output [3:0] out_12,
  output [3:0] out_13,
  output [3:0] out_14,
  output [3:0] out_15
);

  wire [3:0] adder_1_out, adder_2_out, demultiplexer_1_out0, demultiplexer_1_out1, demultiplexer_1_out2,
       demultiplexer_1_out3, multiplexer_1_out, subtractor_1_out;

  Adder #(.width(4)) adder_1 (.a(in_1), .b(in_2), .out(adder_1_out));  // open: cin, cout
  Adder #(.width(4)) adder_2 (.a(in_3), .b(in_4), .out(adder_2_out));  // open: cin, cout
  Adder #(.width(4)) adder_3 (.a(in_5), .b(in_6), .out(adder_2_out));  // open: cin, cout
  Subtractor #(.width(4)) subtractor_1 (.a(in_7), .b(in_11), .out(subtractor_1_out));  // open: bin, bout
  Multiplexer #(.select(2), .width(4)) multiplexer_1 (
    .in0(adder_1_out), .in1(adder_2_out), .in2(adder_2_out), .in3(subtractor_1_out), .out(multiplexer_1_out),
    .sel(in_9), .en(in_8));
  Demultiplexer #(.select(2), .width(4)) demultiplexer_1 (
    .out0(demultiplexer_1_out0), .out1(demultiplexer_1_out1), .out2(demultiplexer_1_out2),
    .out3(demultiplexer_1_out3), .in(multiplexer_1_out), .sel(in_9), .en(in_10));
  Subtractor #(.width(4)) subtractor_2 (.a(demultiplexer_1_out0), .b(in_2), .out(out_12));  // open: bin, bout
  Subtractor #(.width(4)) subtractor_3 (.a(demultiplexer_1_out1), .b(in_4), .out(out_13));  // open: bin, bout
  Subtractor #(.width(4)) subtractor_4 (.a(demultiplexer_1_out2), .b(in_6), .out(out_14));  // open: bin, bout
  Adder #(.width(4)) adder_4 (.a(demultiplexer_1_out3), .b(in_11), .out(out_15));  // open: cin, cout
endmodule
