// Logisim project practical-4.circ as structural Verilog: 1 circuit, main circuit main
module main (
  input  [3:0] in_1,
  input  [3:0] in_2,
  input  [3:0] in_3,
  input  [3:0] in_4,
  input  in_5,
  input  in_6,
  input  in_7,
  output [3:0] out_8,
  output [3:0] out_9
);

  wire [3:0] demultiplexer_1_out0, demultiplexer_1_out1, multiplexer_1_out, xor_1_out, xor_2_out;

  assign xor_1_out = in_1 ^ in_2;  // XOR_Gate xor_1, 4 bits wide
  assign xor_2_out = in_3 ^ in_4;  // XOR_Gate xor_2, 4 bits wide
  Multiplexer #(.width(4)) multiplexer_1 (
    .in0(xor_1_out), .in1(xor_2_out), .out(multiplexer_1_out), .sel(in_5), .en(in_6));
  Demultiplexer #(.width(4)) demultiplexer_1 (
    .out0(demultiplexer_1_out0), .out1(demultiplexer_1_out1), .in(multiplexer_1_out), .sel(in_5), .en(in_7));
  assign out_8 = demultiplexer_1_out0 ^ in_2;  // XOR_Gate xor_3, 4 bits wide
  assign out_9 = demultiplexer_1_out1 ^ in_4;  // XOR_Gate xor_4, 4 bits wide
endmodule
