// Logisim project practical-5 upcounter.circ as structural Verilog: 1 circuit, main circuit main
module main (
  input  in_1,
  input  in_2,
  output out_3,
  output out_4,
  output out_5,
  output out_6
);

  wire and_1_out, and_2_out, j_k_ff_1_qn, j_k_ff_2_qn, j_k_ff_3_qn, j_k_ff_4_qn;

  and and_1 (and_1_out, and_2_out, out_4);
  and and_2 (and_2_out, out_6, out_5);
  J_K_Flip_Flop j_k_ff_1 (
    .J(and_1_out), .clk(in_1), .K(and_1_out), .Q(out_3), .Qn(j_k_ff_1_qn));  // open: preset, en, reset
  J_K_Flip_Flop j_k_ff_2 (
    .J(and_2_out), .clk(in_1), .K(and_2_out), .Q(out_4), .Qn(j_k_ff_2_qn));  // open: preset, en, reset
  J_K_Flip_Flop j_k_ff_3 (.J(out_6), .clk(in_1), .K(out_6), .Q(out_5), .Qn(j_k_ff_3_qn));  // open: preset, en, reset
  J_K_Flip_Flop j_k_ff_4 (.J(in_2), .clk(in_1), .K(in_2), .Q(out_6), .Qn(j_k_ff_4_qn));  // open: preset, en, reset
endmodule
