// Logisim project practical-6.circ as structural Verilog: 1 circuit, main circuit main
module main (
  input  in_1,
  output out_2,
  output out_3,
  output out_4,
  output out_5
);

  wire and_1_out, and_2_out, and_3_out, and_4_out, clock_1_out, or_1_out, t_ff_1_qn, t_ff_2_qn, t_ff_3_qn,
       t_ff_4_qn;

  and and_1 (and_1_out, out_2, out_5);
  and and_2 (and_2_out, and_3_out, out_3);
  or or_1 (or_1_out, and_1_out, and_2_out);
  and and_3 (and_3_out, out_5, out_4);
  and and_4 (and_4_out, t_ff_1_qn, out_5);
  Clock clock_1 (.out(clock_1_out));
  T_Flip_Flop t_ff_1 (.clk(clock_1_out), .T(or_1_out), .Q(out_2), .Qn(t_ff_1_qn));  // open: preset, reset, en
  T_Flip_Flop t_ff_2 (.clk(clock_1_out), .T(and_3_out), .Q(out_3), .Qn(t_ff_2_qn));  // open: preset, reset, en
  T_Flip_Flop t_ff_3 (.clk(clock_1_out), .T(and_4_out), .Q(out_4), .Qn(t_ff_3_qn));  // open: preset, reset, en
  T_Flip_Flop t_ff_4 (.clk(clock_1_out), .T(in_1), .Q(out_5), .Qn(t_ff_4_qn));  // open: preset, reset, en
endmodule
